# Fritzing sketch Ardufarmbot (saved by Fritzing 0.9.3b)
breadboards: 1

parts:
  DHT1 = DHT11 Humitidy and Temperature Sensor
  R1 = Resistor [tolerance=±5% resistance=220 package="2512 [SMD]"]
  LED1 = smd LED [color="Red (633nm)" package="1206 [SMD]"]
  R2 = Resistor [tolerance=±5% resistance=220 package="2512 [SMD]"]
  S1 = Momentary Switch [package=ksa_sealed_tac_switch]
  R3 = Resistor [tolerance=±5% resistance=10k package="2512 [SMD]"]
  Componente1 = Arduino Uno (Rev3) - ICSP
  U4 = 2-Channel 5v Relay Shield [package=relay-2ch5v10a]
  VALVE1 = Plastic Solenoid Valve
  VCC1 = Battery

nets:
  VDD: DHT1.VDD, R1.Pin_1, Componente1.5V, U4.VCC
  N1: DHT1.DATA, R1.Pin_0, Componente1.D5_PWM
  GND: DHT1.GND, R3.Pin_1, Componente1.GND, U4.GND
  N2: LED1.anode, R2.Pin_0
  N3: R2.Pin_1, Componente1.D13/SCK
  N4: S1.1, S1.2
  N5: S1.3, S1.4
  N6: R3.Pin_0, Componente1.D11_PWM/MOSI
  N7: Componente1.D7, U4.IN2
  N8: U4.K2-In, VCC1.+
  N9: U4.K2-On, VALVE1.no_name_yet

custom parts:
  DHT11 Humitidy and Temperature Sensor: DHT11 Humidity and Temperature Sensor
  2-Channel 5v Relay Shield: 2 Channel 5v Relay Shield w. 2x SPD-06VDC-SD-C
